# Fritzing sketch ky037 analog test (saved by Fritzing 0.9.9b)

parts:
  A1 = Esp32-c3 super mini
  Part1 = KY-037 High Sensitivity Sound Detection Module [package="Breakout board"]

nets:
  N1: A1.Pin_2, Part1.A0
  N2: A1.Pin_14, Part1.+
  N3: A1.Pin_15, Part1.G

custom parts:
  Esp32-c3 super mini: ESP32-C3 Development Board ESP32 SuperMini Development Board ESP32 Development Board WiFi Bluetooth.
  KY-037 High Sensitivity Sound Detection Module: KY-037 high sensitivity sound detection module is an analog/digital sensor that uses a condenser microphone to observe changes in environment noise.
